# Fritzing sketch alarmsketch (saved by Fritzing 0.9.3b)

parts:
  MH-Real-Time_Clock_Module_2 = RTC_DS1302_module
  J1 = Piezo Speaker
  hc-sr1 = hc-sr04
  Componente1 = Arduino Uno (Rev3)

nets:
  VCC: MH-Real-Time_Clock_Module_2.VCC, hc-sr1.VCC, Componente1.5V
  GND: MH-Real-Time_Clock_Module_2.GND, J1.pin1, Componente1.GND
  N1: MH-Real-Time_Clock_Module_2.RST, Componente1.D2
  N2: MH-Real-Time_Clock_Module_2.DAT, Componente1.D4
  N3: MH-Real-Time_Clock_Module_2.CLK, Componente1.D5_PWM
  N4: J1.pin2, Componente1.D9_PWM
  N5: hc-sr1.Trig, Componente1.D6_PWM
  N6: hc-sr1.Echo, Componente1.D7

custom parts:
  RTC_DS1302_module: Arduino module DS1302 SPI Real Time Clock
